# Fritzing sketch Conexión ESP32-DHT11 (saved by Fritzing 0.9.3b)
breadboards: 1

parts:
  U1 = ESP32-38PinWide [part_number=ESP32-38PinWide]
  LED1 = LED - 5mm [color="Green (570nm)" package="5 mm [THT]"]
  LED3 = LED - 5mm [color="Red (633nm)" package="5 mm [THT]"]
  LED2 = LED - 5mm [color="Yellow (595nm)" package="5 mm [THT]"]
  R1 = Resistor [tolerance=±5% resistance=330 package=THT]
  R2 = Resistor [tolerance=±5% resistance=330 package=THT]
  LED4 = LED - 5mm [color="Red (633nm)" package="5 mm [THT]"]
  LED5 = LED - 5mm [color="Green (570nm)" package="5 mm [THT]"]
  LED6 = LED - 5mm [color="Yellow (595nm)" package="5 mm [THT]"]
  R3 = Resistor [tolerance=±5% resistance=330 package=THT]
  R4 = Resistor [tolerance=±5% resistance=330 package=THT]
  R5 = Resistor [tolerance=±5% resistance=330 package=THT]
  R6 = Resistor [tolerance=±5% resistance=330 package=THT]
  J1 = DHT11 basic temperature-humidity sensor [form="♂ (male)" package=THT]

nets:
  N1: U1.GPIO35, R6.Pin_0
  N2: U1.GPIO32, R5.Pin_0
  N3: U1.GPIO33, R4.Pin_0
  VIN: U1.VIN, J1.VCC
  N4: U1.GPIO16, J1.OUT
  N5: U1.GPIO19, R1.Pin_0
  N6: U1.GPIO22, R2.Pin_0
  N7: U1.GPIO23, R3.Pin_0
  N8: LED1.cathode, LED3.cathode, LED2.cathode, LED4.cathode, LED5.cathode, LED6.cathode, J1.GND
  N9: LED1.anode, R3.Pin_1
  N10: LED3.anode, R1.Pin_1
  N11: LED2.anode, R2.Pin_1
  N12: LED4.anode, R4.Pin_1
  N13: LED5.anode, R6.Pin_1
  N14: LED6.anode, R5.Pin_1

custom parts:
  ESP32-38PinWide: Generic 38-Pin ESP32 with wide format (only access to one side of pins on a breadboard) based on Stephen Lilley's HiLetgo ESP-WROOM-32 ESP32 ESP-32S Development Board.
  DHT11 basic temperature-humidity sensor: The DHT11 is a basic, ultra low-cost digital temperature and humidity sensor. It uses a capacitive humidity sensor and a thermistor to measure the surrounding air, and spits out a digital signal on the data pin (no analog input pins needed). Its fairly simple to use, but requires careful timing to grab data. The only real downside of this sensor is you can only get new data from it once every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
